# Fritzing sketch FinalFlamingoPCB (saved by Fritzing 0.9.3b)
circuit board: 5.87964cm x 3.96992cm
breadboards: 1

parts:
  +_- = female pin header, 2 pins [form="♀ (female)"]
  I/0 = female pin header, 2 pins [form="♀ (female)"]
  Arduino = Arduino Pro Mini v13
  x_x_x_x_C_R_D_A_L_-_+ = female pin header, 11 pins [form="♀ (female)"]
  +SPK- = Piezo Speaker
  -_D_+ = female pin header, 3 pins [form="♀ (female)"]
  -_+_x_D = female pin header, 4 pins [form="♀ (female)"]
  +_1_2_3_4 = female pin header, 5 pins [form="♀ (female)"]
  10K = Resistor [tolerance=±5% resistance=220 package=THT]
  10K1 = Resistor [tolerance=±5% resistance=220 package=THT]
  10K2 = Resistor [tolerance=±5% resistance=220 package=THT]
  10K3 = Resistor [tolerance=±5% resistance=220 package=THT]

nets:
  N1: +_-.pin1, I/0.pin1, -_D_+.pin3, -_+_x_D.pin2, +_1_2_3_4.pin1
  N2: +_-.pin2, Arduino.GND, x_x_x_x_C_R_D_A_L_-_+.pin2, +SPK-.pin2, -_D_+.pin1, -_+_x_D.pin1, 10K.Pin_1, 10K1.Pin_1, 10K2.Pin_1, 10K3.Pin_1
  N3: I/0.pin2, Arduino.RAW
  N4: Arduino.VCC, x_x_x_x_C_R_D_A_L_-_+.pin1
  N5: Arduino.A1, -_D_+.pin2
  N6: Arduino.A0, -_+_x_D.pin4
  N7: Arduino.D13/SCK, x_x_x_x_C_R_D_A_L_-_+.pin3
  N8: Arduino.D11_PWM/MOSI, x_x_x_x_C_R_D_A_L_-_+.pin4
  N9: Arduino.D10_PWM/SS, x_x_x_x_C_R_D_A_L_-_+.pin7
  N10: Arduino.D9_PWM, x_x_x_x_C_R_D_A_L_-_+.pin6
  N11: Arduino.D8, x_x_x_x_C_R_D_A_L_-_+.pin5
  N12: Arduino.D7, +_1_2_3_4.pin5, 10K1.Pin_0
  N13: Arduino.D6_PWM, +_1_2_3_4.pin4, 10K.Pin_0
  N14: Arduino.D5_PWM, +_1_2_3_4.pin3, 10K2.Pin_0
  N15: Arduino.D4, +_1_2_3_4.pin2, 10K3.Pin_0
  N16: Arduino.D2, +SPK-.pin1

notes:
  Fortune Telling Flamingo
